// Logisim project alu.circ as structural Verilog: 1 circuit, main circuit main
module main (
  input  [3:0] opr_0,
  input  [3:0] opr_1,
  input  En,
  input  [2:0] OP,
  output [3:0] O,
  output ZF,
  output CF,
  output OF_OF,
  output SF
);

  wire adder_1_cout, and_2_out, and_3_out, and_4_out, multiplexer_2_out, nor_1_out, not_1_out, not_2_out,
       subtractor_1_bout;
  wire [3:0] adder_1_out, and_1_out, or_1_out, subtractor_1_out, xor_1_out;

  not not_1 (not_1_out, opr_1[3]);
  Adder #(.width(4)) adder_1 (.a(opr_0), .b(opr_1), .out(adder_1_out), .cout(adder_1_cout));  // open: cin
  Multiplexer multiplexer_1 (.in0(adder_1_cout), .in1(subtractor_1_bout), .out(CF), .sel(OP[0]));
  Subtractor #(.width(4)) subtractor_1 (
    .a(opr_0), .b(opr_1), .out(subtractor_1_out), .bout(subtractor_1_bout));  // open: bin
  assign and_1_out = opr_0 & opr_1;  // AND_Gate and_1, 4 bits wide
  assign or_1_out = opr_0 | opr_1;  // OR_Gate or_1, 4 bits wide
  assign xor_1_out = opr_0 ^ opr_1;  // XOR_Gate xor_1, 4 bits wide
  Multiplexer multiplexer_2 (.in0(opr_1[3]), .in1(not_1_out), .out(multiplexer_2_out), .sel(OP[0]));
  and and_2 (and_2_out, multiplexer_2_out, opr_0[3]);
  nor nor_1 (nor_1_out, multiplexer_2_out, opr_0[3]);
  Multiplexer #(.enable("true"), .select(3), .width(4)) multiplexer_3 (
    .in0(adder_1_out), .in1(subtractor_1_out), .in2(and_1_out), .in3(or_1_out), .in4(xor_1_out), .out(O),
    .sel(OP), .en(En));  // open: in5, in6, in7
  not not_2 (not_2_out, O[3]);
  and and_3 (and_3_out, and_2_out, not_2_out);
  or or_2 (OF_OF, and_3_out, and_4_out);
  and and_4 (and_4_out, O[3], nor_1_out);
  nor nor_2 (ZF, O[0], O[1], O[2], O[3]);

  assign SF = O[3];

  // Notes on the sheet:
  //   Instruction set:
  //   ADD = 000
  //   SUB = 001
  //   AND = 010
  //   OR = 011
  //   X-OR = 100
endmodule
