// Logisim project cpu_design.circ as structural Verilog: 11 circuits, main circuit register_4_bits
module main (
  input  in_1,
  input  in_2,
  input  [1:0] in_3,
  input  in_4,
  input  [3:0] in_5,
  input  in_6,
  input  in_7,
  input  in_8,
  input  [1:0] in_9,
  input  in_10,
  input  in_11,
  input  [3:0] in_12,
  input  in_13,
  input  in_14,
  input  in_15,
  input  in_16,
  input  [1:0] in_17,
  input  in_18,
  input  in_19,
  input  in_20,
  input  [3:0] in_21,
  input  in_22,
  input  in_23,
  input  in_24,
  input  in_25,
  input  in_26,
  input  in_27,
  input  in_28,
  input  in_29,
  input  in_30,
  input  [3:0] in_31,
  input  in_32,
  input  in_33,
  input  in_34,
  input  [3:0] in_35,
  input  in_36,
  input  in_37,
  input  in_38,
  input  [3:0] in_39,
  input  in_40,
  input  in_41,
  input  in_42,
  input  in_43,
  input  in_44,
  input  [3:0] in_45,
  input  [3:0] in_46,
  input  in_47,
  input  in_48,
  input  [3:0] in_49,
  input  in_50,
  input  in_51,
  input  in_52,
  input  in_53,
  input  in_54,
  input  in_55,
  input  in_56,
  output out_57,
  output [3:0] out_58,
  output [3:0] out_59,
  output [1:0] out_60,
  output [1:0] out_61,
  output [3:0] out_62,
  output [1:0] out_63,
  output out_64,
  output [1:0] out_65,
  output [3:0] out_66,
  output [3:0] out_67,
  output out_68,
  output [1:0] out_69,
  output out_70,
  output [3:0] out_71,
  output [3:0] out_72,
  output [3:0] out_73,
  output out_74,
  output out_75,
  output out_76,
  output [3:0] out_77,
  output [3:0] out_78,
  output out_79,
  output [3:0] out_80,
  output out_81,
  output [3:0] out_82,
  output out_83,
  output [3:0] out_84,
  output out_85,
  output [3:0] out_86,
  output [3:0] out_87,
  output [3:0] out_88,
  output [3:0] out_89,
  output [3:0] out_90,
  output out_91,
  output [3:0] out_92,
  output out_93,
  output out_94
);

  wire ACL, ACO_D, ARL, ARO, CLK, En_OP, En_RA, En_RB, not_1_out, not_2_out, not_3_out, not_4_out, not_5_out,
       not_6_out, not_7_out, not_8_out, not_9_out, not_10_out, not_11_out, not_12_out, not_13_out,
       not_14_out, not_15_out, not_16_out, not_17_out, not_18_out, not_19_out, not_20_out, not_21_out,
       not_22_out, not_23_out, not_24_out, not_25_out, PC_INC, PCO, RAM_En, RAM_R_W, W_En_rf;
  wire [1:0] W_addr_rf;

  not not_1 (not_1_out, in_8);
  not not_2 (not_2_out, in_10);
  not not_3 (not_3_out, in_14);
  not not_4 (not_4_out, in_18);
  not not_5 (not_5_out, in_48);
  not not_6 (not_6_out, in_2);
  not not_7 (not_7_out, in_4);
  not not_8 (not_8_out, in_16);
  not not_9 (not_9_out, in_20);
  not not_10 (not_10_out, in_25);
  not not_11 (not_11_out, in_37);
  not not_12 (not_12_out, in_41);
  not not_13 (not_13_out, in_44);
  assign out_67 = not_3_out ? in_12 : 4'bz;  // Controlled_Buffer controlled_buffer_1
  not not_14 (not_14_out, in_22);
  not not_15 (not_15_out, in_28);
  not not_16 (not_16_out, in_30);
  assign out_57 = not_6_out ? in_1 : 1'bz;  // Controlled_Buffer controlled_buffer_2
  assign out_60 = not_7_out ? in_3 : 2'bz;  // Controlled_Buffer controlled_buffer_3
  assign out_64 = in_8 ? En_RB : 1'bz;  // Controlled_Buffer controlled_buffer_4
  assign out_64 = not_1_out ? in_6 : 1'bz;  // Controlled_Buffer controlled_buffer_5
  assign out_65 = in_10 ? out_61 : 2'bz;  // Controlled_Buffer controlled_buffer_6
  assign out_65 = not_2_out ? in_9 : 2'bz;  // Controlled_Buffer controlled_buffer_7
  assign out_67 = in_14 ? out_62 : 4'bz;  // Controlled_Buffer controlled_buffer_8
  assign out_68 = not_8_out ? in_15 : 1'bz;  // Controlled_Buffer controlled_buffer_9
  assign out_69 = in_18 ? W_addr_rf : 2'bz;  // Controlled_Buffer controlled_buffer_10
  assign out_69 = not_4_out ? in_17 : 2'bz;  // Controlled_Buffer controlled_buffer_11
  assign out_70 = not_9_out ? in_19 : 1'bz;  // Controlled_Buffer controlled_buffer_12
  assign out_85 = in_44 ? En_OP : 1'bz;  // Controlled_Buffer controlled_buffer_13
  assign out_85 = not_13_out ? in_43 : 1'bz;  // Controlled_Buffer controlled_buffer_14
  assign out_87 = in_48 ? out_59 : 4'bz;  // Controlled_Buffer controlled_buffer_15
  assign out_87 = not_5_out ? in_46 : 4'bz;  // Controlled_Buffer controlled_buffer_16
  assign out_57 = in_2 ? En_RA : 1'bz;  // Controlled_Buffer controlled_buffer_17
  assign out_60 = in_4 ? out_63 : 2'bz;  // Controlled_Buffer controlled_buffer_18
  assign out_68 = in_16 ? W_En_rf : 1'bz;  // Controlled_Buffer controlled_buffer_19
  assign out_70 = in_20 ? CLK : 1'bz;  // Controlled_Buffer controlled_buffer_20
  assign out_71 = not_14_out ? in_21 : 4'bz;  // Controlled_Buffer controlled_buffer_21
  assign out_74 = in_25 ? ACL : 1'bz;  // Controlled_Buffer controlled_buffer_22
  assign out_74 = not_10_out ? in_23 : 1'bz;  // Controlled_Buffer controlled_buffer_23
  assign out_75 = not_15_out ? in_27 : 1'bz;  // Controlled_Buffer controlled_buffer_24
  assign out_76 = not_16_out ? in_29 : 1'bz;  // Controlled_Buffer controlled_buffer_25
  assign out_80 = in_37 ? out_58 : 4'bz;  // Controlled_Buffer controlled_buffer_26
  assign out_80 = not_11_out ? in_35 : 4'bz;  // Controlled_Buffer controlled_buffer_27
  assign out_84 = in_41 ? out_62 : 4'bz;  // Controlled_Buffer controlled_buffer_28
  assign out_84 = not_12_out ? in_39 : 4'bz;  // Controlled_Buffer controlled_buffer_29
  assign out_71 = in_22 ? out_82 : 4'bz;  // Controlled_Buffer controlled_buffer_30
  assign out_75 = in_28 ? ACO_D : 1'bz;  // Controlled_Buffer controlled_buffer_31
  assign out_76 = in_30 ? CLK : 1'bz;  // Controlled_Buffer controlled_buffer_32
  register_file register_file_1 (
    .RA_En(out_57), .RA_addr(out_60), .RB_En(out_64), .RB_addr(out_65), .Inp(out_67), .W_En(out_68),
    .W_addr(out_69), .clk(out_70), .RA_data(out_58), .RB_data(out_62));
  alu alu_1 (.opr_A(out_80), .opr_B(out_84), .En_OP(out_85), .OP_code({1'b0, out_87[1:0]}), .Result(out_82));
  acc acc_1 (.Inp(out_71), .Wr(out_74), .En_O(out_75), .clk(out_76), .O(out_62));
  Clock u_CLK (.out(CLK));
  falling_edges_counter falling_edges_counter_1 (.RESET(in_11), .INCREMENT(in_13), .CLK(CLK), .O(out_66));
  not not_17 (not_17_out, in_50);
  not not_18 (not_18_out, in_34);
  not not_19 (not_19_out, in_47);
  not not_20 (not_20_out, in_52);
  not not_21 (not_21_out, in_54);
  not not_22 (not_22_out, in_56);
  not not_23 (not_23_out, in_32);
  not not_24 (not_24_out, in_38);
  not not_25 (not_25_out, in_42);
  assign out_89 = in_50 ? out_62 : 4'bz;  // Controlled_Buffer controlled_buffer_33
  assign out_89 = not_17_out ? in_49 : 4'bz;  // Controlled_Buffer controlled_buffer_34
  assign out_79 = in_34 ? ARL : 1'bz;  // Controlled_Buffer controlled_buffer_35
  assign out_79 = not_18_out ? in_33 : 1'bz;  // Controlled_Buffer controlled_buffer_36
  assign out_81 = not_24_out ? in_36 : 1'bz;  // Controlled_Buffer controlled_buffer_37
  assign out_86 = in_47 ? out_73 : 4'bz;  // Controlled_Buffer controlled_buffer_38
  assign out_86 = not_19_out ? in_45 : 4'bz;  // Controlled_Buffer controlled_buffer_39
  assign out_91 = in_52 ? RAM_R_W : 1'bz;  // Controlled_Buffer controlled_buffer_40
  assign out_91 = not_20_out ? in_51 : 1'bz;  // Controlled_Buffer controlled_buffer_41
  assign out_93 = in_54 ? RAM_En : 1'bz;  // Controlled_Buffer controlled_buffer_42
  assign out_93 = not_21_out ? in_53 : 1'bz;  // Controlled_Buffer controlled_buffer_43
  assign out_94 = in_56 ? CLK : 1'bz;  // Controlled_Buffer controlled_buffer_44
  assign out_94 = not_22_out ? in_55 : 1'bz;  // Controlled_Buffer controlled_buffer_45
  assign out_77 = in_32 ? out_62 : 4'bz;  // Controlled_Buffer controlled_buffer_46
  assign out_77 = not_23_out ? in_31 : 4'bz;  // Controlled_Buffer controlled_buffer_47
  assign out_81 = in_38 ? ARO : 1'bz;  // Controlled_Buffer controlled_buffer_48
  assign out_83 = in_42 ? CLK : 1'bz;  // Controlled_Buffer controlled_buffer_49
  assign out_83 = not_25_out ? in_40 : 1'bz;  // Controlled_Buffer controlled_buffer_50
  control_unit control_unit_1 (
    .IR_Ins(out_62), .clk(CLK), .stpc_In(in_5), .stc_reset(in_7), .OP_CODE(out_59), .R1(out_61), .R2(out_63),
    .instuction_low_O(out_62), .RF_LOAD_addr(W_addr_rf), .PC_INC(PC_INC), .PCO(PCO), .RA_En(En_RA),
    .RB_En(En_RB), .ARL(ARL), .ARO(ARO), .W_En_RF(W_En_rf), .En_OP(En_OP), .ACL(ACL), .ACO_D(ACO_D),
    .RAM_R_W(RAM_R_W), .RAM_En(RAM_En));
  PC pc_1 (.Inp(out_62), .PCO(PCO), .PCL(in_24), .Reset(in_26), .PC_INC(PC_INC), .clk(CLK), .O(out_73));
  addr_register addr_register_1 (.Inp(out_77), .LOAD(out_79), .OUT_OUT(out_81), .clk(out_83), .O(out_73));
  ram_16x4 ram_16x4_1 (.addr(out_86), .Inp(out_89), .R_W(out_91), .En(out_93), .RAM_clk(out_94), .O(out_62));

  assign out_72 = out_62;
  assign out_78 = out_73;
  assign out_88 = out_86;
  assign out_90 = out_89;
  assign out_92 = out_62;

  // Other names for the same wires on the sheet: addr_bus[3:0] = out_73; ALU_result[3:0] = out_82;
  //   DATA_BUS[3:0] = out_62; OP_CODE[3:0] = out_59; opr_A[3:0] = out_58; R1[1:0] = out_63; R2[1:0] = out_61
endmodule

module control_unit (
  input  [3:0] IR_Ins,
  input  clk,
  input  [3:0] stpc_In,
  input  stc_reset,
  output [3:0] OP_CODE,
  output [1:0] R1,
  output [1:0] R2,
  output [3:0] instuction_low_O,
  output [1:0] RF_LOAD_addr,
  output PC_INC,
  output PCO,
  output RA_En,
  output RB_En,
  output ARL,
  output ARO,
  output W_En_RF,
  output En_OP,
  output ACL,
  output ACO_D,
  output RAM_R_W,
  output RAM_En
);

  wire ALO_OP_out, decoder_1_out0, decoder_1_out1, decoder_1_out2, decoder_1_out3, DN, IHL, ILL,
       instuctino_low_O, LOAD_0_out, LOAD_1_out, LOAD_out, not_1_out, OP_out, STOR_0_out, STOR_1_out,
       STOR_out;
  wire [3:0] step_counter_1_o;

  register_4_bits register_4_bits_1 (.Inp(IR_Ins), .S(IHL), .clk(clk), .O(OP_CODE));
  register_4_bits register_4_bits_2 (.Inp(IR_Ins), .S(ILL), .clk(clk), .O({R1, R2}));
  not not_1 (not_1_out, OP_CODE[2]);
  assign instuction_low_O = instuctino_low_O ? {R1, R2} : 4'bz;  // Controlled_Buffer controlled_buffer_1
  nor OP (OP_out, OP_CODE[2], OP_CODE[3]);
  and LOAD (LOAD_out, not_1_out, OP_CODE[3]);
  and STOR (STOR_out, OP_CODE[2], OP_CODE[3]);
  assign RF_LOAD_addr = LOAD_1_out ? OP_CODE[1:0] : 2'bz;  // Controlled_Buffer controlled_buffer_2
  step_counter step_counter_1 (.Inp(stpc_In), .S(DN), .clk(clk), .R(stc_reset), .O(step_counter_1_o));
  Decoder #(.select(4)) decoder_1 (
    .out0(decoder_1_out0), .out1(decoder_1_out1), .out2(decoder_1_out2), .out3(decoder_1_out3),
    .sel(step_counter_1_o));  // open: out4, out5, out6, out7, out8, out9, out10, out11, out12, out13, out14, out15, en
  and ALO_OP (ALO_OP_out, decoder_1_out2, OP_out);
  and LOAD_0 (LOAD_0_out, decoder_1_out2, LOAD_out);
  and LOAD_1 (LOAD_1_out, decoder_1_out3, LOAD_out);
  and STOR_0 (STOR_0_out, decoder_1_out2, STOR_out);
  and STOR_1 (STOR_1_out, decoder_1_out3, STOR_out);
  or or_1 (instuctino_low_O, STOR_0_out, LOAD_0_out);
  or or_2 (PC_INC, decoder_1_out0, decoder_1_out1);
  or or_3 (PCO, decoder_1_out0, decoder_1_out1);
  buf or_4 (RA_En, ALO_OP_out);  // OR_Gate
  buf or_5 (RB_En, ALO_OP_out);  // OR_Gate
  or or_6 (ARL, STOR_0_out, LOAD_0_out);
  or or_7 (ARO, STOR_1_out, LOAD_1_out);
  buf or_8 (W_En_RF, LOAD_1_out);  // OR_Gate
  buf or_9 (En_OP, ALO_OP_out);  // OR_Gate
  buf or_10 (ACL, ALO_OP_out);  // OR_Gate
  buf or_11 (ACO_D, STOR_1_out);  // OR_Gate
  buf or_12 (IHL, decoder_1_out0);  // OR_Gate
  buf or_13 (ILL, decoder_1_out1);  // OR_Gate
  or or_14 (RAM_R_W, decoder_1_out0, decoder_1_out1, LOAD_1_out);
  or or_15 (RAM_En, decoder_1_out0, decoder_1_out1, STOR_1_out, LOAD_1_out);
  or or_16 (DN, STOR_1_out, LOAD_1_out, ALO_OP_out);

  // Notes on the sheet:
  //   instruction:
  //   xx
  //   00:ALU OP
  //   10: LOAD
  //   01: pending
  //   11:STOR
  //   xx
  //   ALU op:
  //   00:ADD
  //   10: SUB
  //   01: AND
  //   11: OR
  //   LOAD : register addrisse
  //   xxxx
  //   STOR: 4-bits RAM addr
  //   ALU OP: 2-nits each RF addr
  //   LOAD: 2-micro instruction: RAM -> MDR -> RF
endmodule

module step_counter (
  input  [3:0] Inp,
  input  S,
  input  clk,
  input  R,
  output [3:0] O
);

  wire multiplexer_1_out, multiplexer_2_out, multiplexer_3_out, multiplexer_4_out;
  wire [3:0] adder_1_out;

  D_Flip_Flop #(.trigger("falling")) d_ff_1 (
    .D(multiplexer_1_out), .clk(clk), .Q(O[3]), .preset(1'b0), .reset(R));  // open: Qn
  Multiplexer multiplexer_1 (.in0(adder_1_out[3]), .in1(Inp[3]), .out(multiplexer_1_out), .sel(S));
  Multiplexer multiplexer_2 (.in0(adder_1_out[2]), .in1(Inp[2]), .out(multiplexer_2_out), .sel(S));
  D_Flip_Flop #(.trigger("falling")) d_ff_2 (
    .D(multiplexer_2_out), .clk(clk), .Q(O[2]), .preset(1'b0), .reset(R));  // open: Qn
  Multiplexer multiplexer_3 (.in0(adder_1_out[1]), .in1(Inp[1]), .out(multiplexer_3_out), .sel(S));
  D_Flip_Flop #(.trigger("falling")) d_ff_3 (
    .D(multiplexer_3_out), .clk(clk), .Q(O[1]), .preset(1'b0), .reset(R));  // open: Qn
  Adder #(.width(4)) adder_1 (.a(O), .b(4'b0000), .out(adder_1_out), .cin(1'b1));  // open: cout
  Multiplexer multiplexer_4 (.in0(adder_1_out[0]), .in1(Inp[0]), .out(multiplexer_4_out), .sel(S));
  D_Flip_Flop #(.trigger("falling")) d_ff_4 (
    .D(multiplexer_4_out), .clk(clk), .Q(O[0]), .preset(1'b0), .reset(R));  // open: Qn
endmodule

module ram_16x4 (
  input  [3:0] addr,
  input  [3:0] Inp,
  input  R_W,
  input  En,
  input  RAM_clk,
  output [3:0] O
);

  wire and_1_out, and_2_out, and_3_out, and_4_out, and_5_out, and_6_out, and_7_out, and_8_out, and_9_out,
       and_10_out, and_11_out, and_12_out, and_13_out, and_14_out, and_15_out, and_16_out, and_17_out,
       and_18_out, and_19_out, and_20_out, and_21_out, and_22_out, and_23_out, and_24_out, and_25_out,
       and_26_out, and_27_out, and_28_out, and_29_out, and_30_out, and_31_out, and_32_out, and_33_out,
       and_34_out, decoder_1_out0, decoder_1_out1, decoder_1_out2, decoder_1_out3, decoder_2_out0,
       decoder_2_out1, decoder_2_out2, decoder_2_out3, decoder_3_out0, decoder_3_out1, decoder_3_out2,
       decoder_3_out3, decoder_4_out0, decoder_4_out1, decoder_4_out2, decoder_4_out3, not_1_out;
  wire [3:0] register_4_bits_1_o, register_4_bits_2_o, register_4_bits_3_o, register_4_bits_4_o,
       register_4_bits_5_o, register_4_bits_6_o, register_4_bits_7_o, register_4_bits_8_o,
       register_4_bits_9_o, register_4_bits_10_o, register_4_bits_11_o, register_4_bits_12_o,
       register_4_bits_13_o, register_4_bits_14_o, register_4_bits_15_o, register_4_bits_16_o;

  not not_1 (not_1_out, R_W);
  and and_1 (and_1_out, not_1_out, En);
  and and_2 (and_2_out, R_W, En);
  Decoder #(.select(2)) decoder_1 (
    .out0(decoder_1_out0), .out1(decoder_1_out1), .out2(decoder_1_out2), .out3(decoder_1_out3),
    .sel(addr[3:2]), .en(and_2_out));
  Decoder #(.select(2)) decoder_2 (
    .out0(decoder_2_out0), .out1(decoder_2_out1), .out2(decoder_2_out2), .out3(decoder_2_out3),
    .sel(addr[3:2]), .en(and_1_out));
  and and_3 (and_3_out, decoder_3_out0, decoder_2_out0);
  and and_4 (and_4_out, decoder_3_out0, decoder_2_out1);
  and and_5 (and_5_out, decoder_3_out0, decoder_2_out2);
  and and_6 (and_6_out, decoder_3_out0, decoder_2_out3);
  register_4_bits register_4_bits_1 (.Inp(Inp), .S(and_3_out), .clk(RAM_clk), .O(register_4_bits_1_o));
  register_4_bits register_4_bits_2 (.Inp(Inp), .S(and_4_out), .clk(RAM_clk), .O(register_4_bits_2_o));
  register_4_bits register_4_bits_3 (.Inp(Inp), .S(and_5_out), .clk(RAM_clk), .O(register_4_bits_3_o));
  register_4_bits register_4_bits_4 (.Inp(Inp), .S(and_6_out), .clk(RAM_clk), .O(register_4_bits_4_o));
  assign O = and_7_out ? register_4_bits_1_o : 4'bz;  // Controlled_Buffer controlled_buffer_1
  and and_7 (and_7_out, decoder_4_out0, decoder_1_out0);
  assign O = and_8_out ? register_4_bits_2_o : 4'bz;  // Controlled_Buffer controlled_buffer_2
  and and_8 (and_8_out, decoder_4_out0, decoder_1_out1);
  assign O = and_9_out ? register_4_bits_3_o : 4'bz;  // Controlled_Buffer controlled_buffer_3
  and and_9 (and_9_out, decoder_4_out0, decoder_1_out2);
  assign O = and_10_out ? register_4_bits_4_o : 4'bz;  // Controlled_Buffer controlled_buffer_4
  and and_10 (and_10_out, decoder_4_out0, decoder_1_out3);
  Decoder #(.select(2)) decoder_3 (
    .out0(decoder_3_out0), .out1(decoder_3_out1), .out2(decoder_3_out2), .out3(decoder_3_out3),
    .sel(addr[1:0]), .en(and_1_out));
  and and_11 (and_11_out, decoder_3_out1, decoder_2_out0);
  and and_12 (and_12_out, decoder_3_out1, decoder_2_out1);
  and and_13 (and_13_out, decoder_3_out1, decoder_2_out2);
  and and_14 (and_14_out, decoder_3_out1, decoder_2_out3);
  Decoder #(.select(2)) decoder_4 (
    .out0(decoder_4_out0), .out1(decoder_4_out1), .out2(decoder_4_out2), .out3(decoder_4_out3),
    .sel(addr[1:0]), .en(and_2_out));
  register_4_bits register_4_bits_5 (.Inp(Inp), .S(and_11_out), .clk(RAM_clk), .O(register_4_bits_5_o));
  register_4_bits register_4_bits_6 (.Inp(Inp), .S(and_12_out), .clk(RAM_clk), .O(register_4_bits_6_o));
  register_4_bits register_4_bits_7 (.Inp(Inp), .S(and_13_out), .clk(RAM_clk), .O(register_4_bits_7_o));
  register_4_bits register_4_bits_8 (.Inp(Inp), .S(and_14_out), .clk(RAM_clk), .O(register_4_bits_8_o));
  assign O = and_15_out ? register_4_bits_5_o : 4'bz;  // Controlled_Buffer controlled_buffer_5
  and and_15 (and_15_out, decoder_4_out1, decoder_1_out0);
  assign O = and_16_out ? register_4_bits_6_o : 4'bz;  // Controlled_Buffer controlled_buffer_6
  and and_16 (and_16_out, decoder_4_out1, decoder_1_out1);
  assign O = and_17_out ? register_4_bits_7_o : 4'bz;  // Controlled_Buffer controlled_buffer_7
  and and_17 (and_17_out, decoder_4_out1, decoder_1_out2);
  assign O = and_18_out ? register_4_bits_8_o : 4'bz;  // Controlled_Buffer controlled_buffer_8
  and and_18 (and_18_out, decoder_4_out1, decoder_1_out3);
  and and_19 (and_19_out, decoder_3_out2, decoder_2_out0);
  and and_20 (and_20_out, decoder_3_out2, decoder_2_out1);
  and and_21 (and_21_out, decoder_3_out2, decoder_2_out2);
  and and_22 (and_22_out, decoder_3_out2, decoder_2_out3);
  register_4_bits register_4_bits_9 (.Inp(Inp), .S(and_19_out), .clk(RAM_clk), .O(register_4_bits_9_o));
  register_4_bits register_4_bits_10 (.Inp(Inp), .S(and_20_out), .clk(RAM_clk), .O(register_4_bits_10_o));
  register_4_bits register_4_bits_11 (.Inp(Inp), .S(and_21_out), .clk(RAM_clk), .O(register_4_bits_11_o));
  register_4_bits register_4_bits_12 (.Inp(Inp), .S(and_22_out), .clk(RAM_clk), .O(register_4_bits_12_o));
  assign O = and_23_out ? register_4_bits_9_o : 4'bz;  // Controlled_Buffer controlled_buffer_9
  and and_23 (and_23_out, decoder_4_out2, decoder_1_out0);
  assign O = and_24_out ? register_4_bits_10_o : 4'bz;  // Controlled_Buffer controlled_buffer_10
  and and_24 (and_24_out, decoder_4_out2, decoder_1_out1);
  assign O = and_25_out ? register_4_bits_11_o : 4'bz;  // Controlled_Buffer controlled_buffer_11
  and and_25 (and_25_out, decoder_4_out2, decoder_1_out2);
  assign O = and_26_out ? register_4_bits_12_o : 4'bz;  // Controlled_Buffer controlled_buffer_12
  and and_26 (and_26_out, decoder_4_out2, decoder_1_out3);
  and and_27 (and_27_out, decoder_3_out3, decoder_2_out0);
  and and_28 (and_28_out, decoder_3_out3, decoder_2_out1);
  and and_29 (and_29_out, decoder_3_out3, decoder_2_out2);
  and and_30 (and_30_out, decoder_3_out3, decoder_2_out3);
  register_4_bits register_4_bits_13 (.Inp(Inp), .S(and_27_out), .clk(RAM_clk), .O(register_4_bits_13_o));
  register_4_bits register_4_bits_14 (.Inp(Inp), .S(and_28_out), .clk(RAM_clk), .O(register_4_bits_14_o));
  register_4_bits register_4_bits_15 (.Inp(Inp), .S(and_29_out), .clk(RAM_clk), .O(register_4_bits_15_o));
  register_4_bits register_4_bits_16 (.Inp(Inp), .S(and_30_out), .clk(RAM_clk), .O(register_4_bits_16_o));
  assign O = and_31_out ? register_4_bits_13_o : 4'bz;  // Controlled_Buffer controlled_buffer_13
  and and_31 (and_31_out, decoder_4_out3, decoder_1_out0);
  assign O = and_32_out ? register_4_bits_14_o : 4'bz;  // Controlled_Buffer controlled_buffer_14
  and and_32 (and_32_out, decoder_4_out3, decoder_1_out1);
  assign O = and_33_out ? register_4_bits_15_o : 4'bz;  // Controlled_Buffer controlled_buffer_15
  and and_33 (and_33_out, decoder_4_out3, decoder_1_out2);
  assign O = and_34_out ? register_4_bits_16_o : 4'bz;  // Controlled_Buffer controlled_buffer_16
  and and_34 (and_34_out, decoder_4_out3, decoder_1_out3);
endmodule

module addr_register (
  input  [3:0] Inp,
  input  LOAD,
  input  OUT_OUT,
  input  clk,
  output [3:0] O
);

  wire multiplexer_1_out, multiplexer_2_out, multiplexer_3_out, multiplexer_4_out;
  wire [3:0] d_ff_4_q;

  D_Flip_Flop #(.trigger("falling")) d_ff_1 (
    .D(multiplexer_1_out), .clk(clk), .Q(d_ff_4_q[3]), .preset(1'b0), .reset(1'b0));  // open: Qn
  Multiplexer multiplexer_1 (.in0(d_ff_4_q[3]), .in1(Inp[3]), .out(multiplexer_1_out), .sel(LOAD));
  Multiplexer multiplexer_2 (.in0(d_ff_4_q[2]), .in1(Inp[2]), .out(multiplexer_2_out), .sel(LOAD));
  D_Flip_Flop #(.trigger("falling")) d_ff_2 (
    .D(multiplexer_2_out), .clk(clk), .Q(d_ff_4_q[2]), .preset(1'b0), .reset(1'b0));  // open: Qn
  Multiplexer multiplexer_3 (.in0(d_ff_4_q[1]), .in1(Inp[1]), .out(multiplexer_3_out), .sel(LOAD));
  assign O = OUT_OUT ? d_ff_4_q : 4'bz;  // Controlled_Buffer controlled_buffer_1
  D_Flip_Flop #(.trigger("falling")) d_ff_3 (
    .D(multiplexer_3_out), .clk(clk), .Q(d_ff_4_q[1]), .preset(1'b0), .reset(1'b0));  // open: Qn
  Multiplexer multiplexer_4 (.in0(d_ff_4_q[0]), .in1(Inp[0]), .out(multiplexer_4_out), .sel(LOAD));
  D_Flip_Flop #(.trigger("falling")) d_ff_4 (
    .D(multiplexer_4_out), .clk(clk), .Q(d_ff_4_q[0]), .preset(1'b0), .reset(1'b0));  // open: Qn
endmodule

module register_file (
  input  RA_En,
  input  [1:0] RA_addr,
  input  RB_En,
  input  [1:0] RB_addr,
  input  [3:0] Inp,
  input  W_En,
  input  [1:0] W_addr,
  input  clk,
  output [3:0] RA_data,
  output [3:0] RB_data
);

  wire decoder_1_out0, decoder_1_out1, decoder_1_out2, decoder_1_out3, decoder_2_out0, decoder_2_out1,
       decoder_2_out2, decoder_2_out3, decoder_3_out0, decoder_3_out1, decoder_3_out2, decoder_3_out3;
  wire [3:0] register_4_bits_1_o, register_4_bits_2_o, register_4_bits_3_o, register_4_bits_4_o;

  Decoder #(.select(2)) decoder_1 (
    .out0(decoder_1_out0), .out1(decoder_1_out1), .out2(decoder_1_out2), .out3(decoder_1_out3), .sel(W_addr),
    .en(W_En));
  Decoder #(.select(2)) decoder_2 (
    .out0(decoder_2_out0), .out1(decoder_2_out1), .out2(decoder_2_out2), .out3(decoder_2_out3),
    .sel(RA_addr), .en(RA_En));
  register_4_bits register_4_bits_1 (.Inp(Inp), .S(decoder_1_out0), .clk(clk), .O(register_4_bits_1_o));
  register_4_bits register_4_bits_2 (.Inp(Inp), .S(decoder_1_out1), .clk(clk), .O(register_4_bits_2_o));
  register_4_bits register_4_bits_3 (.Inp(Inp), .S(decoder_1_out2), .clk(clk), .O(register_4_bits_3_o));
  register_4_bits register_4_bits_4 (.Inp(Inp), .S(decoder_1_out3), .clk(clk), .O(register_4_bits_4_o));
  assign RA_data = decoder_2_out0 ? register_4_bits_1_o : 4'bz;  // Controlled_Buffer controlled_buffer_1
  assign RA_data = decoder_2_out1 ? register_4_bits_2_o : 4'bz;  // Controlled_Buffer controlled_buffer_2
  assign RA_data = decoder_2_out2 ? register_4_bits_3_o : 4'bz;  // Controlled_Buffer controlled_buffer_3
  assign RA_data = decoder_2_out3 ? register_4_bits_4_o : 4'bz;  // Controlled_Buffer controlled_buffer_4
  assign RB_data = decoder_3_out0 ? register_4_bits_1_o : 4'bz;  // Controlled_Buffer controlled_buffer_5
  assign RB_data = decoder_3_out1 ? register_4_bits_2_o : 4'bz;  // Controlled_Buffer controlled_buffer_6
  assign RB_data = decoder_3_out2 ? register_4_bits_3_o : 4'bz;  // Controlled_Buffer controlled_buffer_7
  assign RB_data = decoder_3_out3 ? register_4_bits_4_o : 4'bz;  // Controlled_Buffer controlled_buffer_8
  Decoder #(.select(2)) decoder_3 (
    .out0(decoder_3_out0), .out1(decoder_3_out1), .out2(decoder_3_out2), .out3(decoder_3_out3),
    .sel(RB_addr), .en(RB_En));
endmodule

module alu (
  input  [3:0] opr_A,
  input  [3:0] opr_B,
  input  En_OP,
  input  [2:0] OP_code,
  output [3:0] Result
);

  wire [3:0] adder_1_out, and_1_out, multiplexer_1_out, or_1_out, subtractor_1_out, xor_1_out;

  Adder #(.width(4)) adder_1 (.a(opr_A), .b(opr_B), .out(adder_1_out));  // open: cin, cout
  Subtractor #(.width(4)) subtractor_1 (.a(opr_A), .b(opr_B), .out(subtractor_1_out));  // open: bin, bout
  assign and_1_out = opr_A & opr_B;  // AND_Gate and_1, 4 bits wide
  assign or_1_out = opr_A | opr_B;  // OR_Gate or_1, 4 bits wide
  assign xor_1_out = opr_A ^ opr_B;  // XOR_Gate xor_1, 4 bits wide
  Multiplexer #(.select(3), .width(4)) multiplexer_1 (
    .in0(adder_1_out), .in1(subtractor_1_out), .in2(and_1_out), .in3(or_1_out), .in4(xor_1_out),
    .out(multiplexer_1_out), .sel(OP_code));  // open: in5, in6, in7
  Multiplexer #(.width(4)) multiplexer_2 (.in0(opr_B), .in1(multiplexer_1_out), .out(Result), .sel(En_OP));

  // Notes on the sheet:
  //   Instruction set:
  //   ADD = 000
  //   SUB = 001
  //   AND = 010
  //   OR = 011
  //   pending: X-OR = 100
endmodule

module acc (
  input  [3:0] Inp,
  input  Wr,
  input  En_O,
  input  clk,
  output [3:0] O
);

  wire multiplexer_1_out, multiplexer_2_out, multiplexer_3_out, multiplexer_4_out;
  wire [3:0] d_ff_4_q;

  D_Flip_Flop #(.trigger("falling")) d_ff_1 (
    .D(multiplexer_1_out), .clk(clk), .Q(d_ff_4_q[3]), .preset(1'b0), .reset(1'b0));  // open: Qn
  Multiplexer multiplexer_1 (.in0(d_ff_4_q[3]), .in1(Inp[3]), .out(multiplexer_1_out), .sel(Wr));
  Multiplexer multiplexer_2 (.in0(d_ff_4_q[2]), .in1(Inp[2]), .out(multiplexer_2_out), .sel(Wr));
  D_Flip_Flop #(.trigger("falling")) d_ff_2 (
    .D(multiplexer_2_out), .clk(clk), .Q(d_ff_4_q[2]), .preset(1'b0), .reset(1'b0));  // open: Qn
  Multiplexer multiplexer_3 (.in0(d_ff_4_q[1]), .in1(Inp[1]), .out(multiplexer_3_out), .sel(Wr));
  assign O = En_O ? d_ff_4_q : 4'bz;  // Controlled_Buffer controlled_buffer_1
  D_Flip_Flop #(.trigger("falling")) d_ff_3 (
    .D(multiplexer_3_out), .clk(clk), .Q(d_ff_4_q[1]), .preset(1'b0), .reset(1'b0));  // open: Qn
  Multiplexer multiplexer_4 (.in0(d_ff_4_q[0]), .in1(Inp[0]), .out(multiplexer_4_out), .sel(Wr));
  D_Flip_Flop #(.trigger("falling")) d_ff_4 (
    .D(multiplexer_4_out), .clk(clk), .Q(d_ff_4_q[0]), .preset(1'b0), .reset(1'b0));  // open: Qn
endmodule

module PC (
  input  [3:0] Inp,
  input  PCO,
  input  PCL,
  input  Reset,
  input  PC_INC,
  input  clk,
  output [3:0] O
);

  wire and_1_out, multiplexer_1_out, multiplexer_2_out, multiplexer_3_out, multiplexer_4_out;
  wire [3:0] adder_1_out, d_ff_4_q;

  and and_1 (and_1_out, PC_INC, clk);
  D_Flip_Flop #(.trigger("falling")) d_ff_1 (
    .D(multiplexer_1_out), .clk(and_1_out), .Q(d_ff_4_q[3]), .preset(1'b0), .reset(Reset));  // open: Qn
  Multiplexer multiplexer_1 (.in0(adder_1_out[3]), .in1(Inp[3]), .out(multiplexer_1_out), .sel(PCL));
  Multiplexer multiplexer_2 (.in0(adder_1_out[2]), .in1(Inp[2]), .out(multiplexer_2_out), .sel(PCL));
  D_Flip_Flop #(.trigger("falling")) d_ff_2 (
    .D(multiplexer_2_out), .clk(and_1_out), .Q(d_ff_4_q[2]), .preset(1'b0), .reset(Reset));  // open: Qn
  assign O = PCO ? d_ff_4_q : 4'bz;  // Controlled_Buffer controlled_buffer_1
  Multiplexer multiplexer_3 (.in0(adder_1_out[1]), .in1(Inp[1]), .out(multiplexer_3_out), .sel(PCL));
  D_Flip_Flop #(.trigger("falling")) d_ff_3 (
    .D(multiplexer_3_out), .clk(and_1_out), .Q(d_ff_4_q[1]), .preset(1'b0), .reset(Reset));  // open: Qn
  Adder #(.width(4)) adder_1 (.a(d_ff_4_q), .b(4'b0000), .out(adder_1_out), .cin(1'b1));  // open: cout
  Multiplexer multiplexer_4 (.in0(adder_1_out[0]), .in1(Inp[0]), .out(multiplexer_4_out), .sel(PCL));
  D_Flip_Flop #(.trigger("falling")) d_ff_4 (
    .D(multiplexer_4_out), .clk(and_1_out), .Q(d_ff_4_q[0]), .preset(1'b0), .reset(Reset));  // open: Qn
endmodule

module register_4_bits (
  input  [3:0] Inp,
  input  S,
  input  clk,
  output [3:0] O
);

  wire multiplexer_1_out, multiplexer_2_out, multiplexer_3_out, multiplexer_4_out;

  D_Flip_Flop #(.trigger("falling")) d_ff_1 (
    .D(multiplexer_1_out), .clk(clk), .Q(O[3]), .preset(1'b0), .reset(1'b0));  // open: Qn
  Multiplexer multiplexer_1 (.in0(O[3]), .in1(Inp[3]), .out(multiplexer_1_out), .sel(S));
  Multiplexer multiplexer_2 (.in0(O[2]), .in1(Inp[2]), .out(multiplexer_2_out), .sel(S));
  D_Flip_Flop #(.trigger("falling")) d_ff_2 (
    .D(multiplexer_2_out), .clk(clk), .Q(O[2]), .preset(1'b0), .reset(1'b0));  // open: Qn
  Multiplexer multiplexer_3 (.in0(O[1]), .in1(Inp[1]), .out(multiplexer_3_out), .sel(S));
  D_Flip_Flop #(.trigger("falling")) d_ff_3 (
    .D(multiplexer_3_out), .clk(clk), .Q(O[1]), .preset(1'b0), .reset(1'b0));  // open: Qn
  Multiplexer multiplexer_4 (.in0(O[0]), .in1(Inp[0]), .out(multiplexer_4_out), .sel(S));
  D_Flip_Flop #(.trigger("falling")) d_ff_4 (
    .D(multiplexer_4_out), .clk(clk), .Q(O[0]), .preset(1'b0), .reset(1'b0));  // open: Qn
endmodule

module falling_edges_counter (
  input  RESET,
  input  INCREMENT,
  input  CLK,
  output [3:0] O
);

  PC pc_1 (.PCO(1'b1), .Reset(RESET), .PC_INC(INCREMENT), .clk(CLK), .O(O));  // open: Inp, PCL
endmodule
