// Logisim project basic_rams.circ as structural Verilog: 6 circuits, main circuit main
module main (
);

  RAM_4x4 ram_4x4_1 ();  // open: I_3, I_2, I_1, I_0, AD_En, RAM_AD
  ram_4x2 ram_4x2_1 ();  // open: In_1, In_0, AD_En, AD
  ram_2x1 ram_2x1_1 ();  // open: I, AD_En, AD
  ram_1bit ram_1bit_1 ();  // open: in_1, in_2, in_3, in_4
  ram_4x1 ram_4x1_1 ();  // open: I, AD_En, RAM_ad, O_0, O_1, O_2, O_3
endmodule

module RAM_4x4 (
  input  I_3,
  input  I_2,
  input  I_1,
  input  I_0,
  input  AD_En,
  input  [1:0] RAM_AD
);

  wire d_ff_1_q, d_ff_2_q, d_ff_3_q, d_ff_4_q, d_ff_5_q, d_ff_6_q, d_ff_7_q, d_ff_8_q, d_ff_9_q, d_ff_10_q,
       d_ff_11_q, d_ff_12_q, d_ff_13_q, d_ff_14_q, d_ff_15_q, d_ff_16_q, decoder_1_out0, decoder_1_out1,
       decoder_1_out2, decoder_1_out3, multiplexer_1_out, multiplexer_2_out, multiplexer_3_out,
       multiplexer_4_out, multiplexer_5_out, multiplexer_6_out, multiplexer_7_out, multiplexer_8_out,
       multiplexer_9_out, multiplexer_10_out, multiplexer_11_out, multiplexer_12_out, multiplexer_13_out,
       multiplexer_14_out, multiplexer_15_out, multiplexer_16_out, RAM_clk_out;

  Decoder #(.select(2)) decoder_1 (
    .out0(decoder_1_out0), .out1(decoder_1_out1), .out2(decoder_1_out2), .out3(decoder_1_out3), .sel(RAM_AD),
    .en(AD_En));
  Clock RAM_clk (.out(RAM_clk_out));
  Multiplexer multiplexer_1 (.in0(d_ff_1_q), .in1(I_3), .out(multiplexer_1_out), .sel(decoder_1_out0));
  Multiplexer multiplexer_2 (.in0(d_ff_2_q), .in1(I_3), .out(multiplexer_2_out), .sel(decoder_1_out1));
  Multiplexer multiplexer_3 (.in0(d_ff_3_q), .in1(I_3), .out(multiplexer_3_out), .sel(decoder_1_out2));
  Multiplexer multiplexer_4 (.in0(d_ff_4_q), .in1(I_3), .out(multiplexer_4_out), .sel(decoder_1_out3));
  D_Flip_Flop #(.trigger("falling")) d_ff_1 (
    .D(multiplexer_1_out), .clk(RAM_clk_out), .Q(d_ff_1_q));  // open: Qn, preset, reset
  D_Flip_Flop #(.trigger("falling")) d_ff_2 (
    .D(multiplexer_2_out), .clk(RAM_clk_out), .Q(d_ff_2_q));  // open: Qn, preset, reset
  D_Flip_Flop #(.trigger("falling")) d_ff_3 (
    .D(multiplexer_3_out), .clk(RAM_clk_out), .Q(d_ff_3_q));  // open: Qn, preset, reset
  D_Flip_Flop #(.trigger("falling")) d_ff_4 (
    .D(multiplexer_4_out), .clk(RAM_clk_out), .Q(d_ff_4_q));  // open: Qn, preset, reset
  LED led_1 (.in(d_ff_1_q));
  LED led_2 (.in(d_ff_2_q));
  LED led_3 (.in(d_ff_3_q));
  LED led_4 (.in(d_ff_4_q));
  Multiplexer multiplexer_5 (.in0(d_ff_5_q), .in1(I_2), .out(multiplexer_5_out), .sel(decoder_1_out0));
  Multiplexer multiplexer_6 (.in0(d_ff_6_q), .in1(I_2), .out(multiplexer_6_out), .sel(decoder_1_out1));
  Multiplexer multiplexer_7 (.in0(d_ff_7_q), .in1(I_2), .out(multiplexer_7_out), .sel(decoder_1_out2));
  Multiplexer multiplexer_8 (.in0(d_ff_8_q), .in1(I_2), .out(multiplexer_8_out), .sel(decoder_1_out3));
  D_Flip_Flop #(.trigger("falling")) d_ff_5 (
    .D(multiplexer_5_out), .clk(RAM_clk_out), .Q(d_ff_5_q));  // open: Qn, preset, reset
  D_Flip_Flop #(.trigger("falling")) d_ff_6 (
    .D(multiplexer_6_out), .clk(RAM_clk_out), .Q(d_ff_6_q));  // open: Qn, preset, reset
  D_Flip_Flop #(.trigger("falling")) d_ff_7 (
    .D(multiplexer_7_out), .clk(RAM_clk_out), .Q(d_ff_7_q));  // open: Qn, preset, reset
  D_Flip_Flop #(.trigger("falling")) d_ff_8 (
    .D(multiplexer_8_out), .clk(RAM_clk_out), .Q(d_ff_8_q));  // open: Qn, preset, reset
  LED led_5 (.in(d_ff_5_q));
  LED led_6 (.in(d_ff_6_q));
  LED led_7 (.in(d_ff_7_q));
  LED led_8 (.in(d_ff_8_q));
  D_Flip_Flop #(.trigger("falling")) d_ff_9 (
    .D(multiplexer_9_out), .clk(RAM_clk_out), .Q(d_ff_9_q));  // open: Qn, preset, reset
  Multiplexer multiplexer_9 (.in0(d_ff_9_q), .in1(I_1), .out(multiplexer_9_out), .sel(decoder_1_out0));
  D_Flip_Flop #(.trigger("falling")) d_ff_10 (
    .D(multiplexer_10_out), .clk(RAM_clk_out), .Q(d_ff_10_q));  // open: Qn, preset, reset
  Multiplexer multiplexer_10 (.in0(d_ff_10_q), .in1(I_1), .out(multiplexer_10_out), .sel(decoder_1_out1));
  D_Flip_Flop #(.trigger("falling")) d_ff_11 (
    .D(multiplexer_11_out), .clk(RAM_clk_out), .Q(d_ff_11_q));  // open: Qn, preset, reset
  Multiplexer multiplexer_11 (.in0(d_ff_11_q), .in1(I_1), .out(multiplexer_11_out), .sel(decoder_1_out2));
  D_Flip_Flop #(.trigger("falling")) d_ff_12 (
    .D(multiplexer_12_out), .clk(RAM_clk_out), .Q(d_ff_12_q));  // open: Qn, preset, reset
  Multiplexer multiplexer_12 (.in0(d_ff_12_q), .in1(I_1), .out(multiplexer_12_out), .sel(decoder_1_out3));
  LED led_9 (.in(d_ff_9_q));
  LED led_10 (.in(d_ff_10_q));
  LED led_11 (.in(d_ff_11_q));
  LED led_12 (.in(d_ff_12_q));
  D_Flip_Flop #(.trigger("falling")) d_ff_13 (
    .D(multiplexer_13_out), .clk(RAM_clk_out), .Q(d_ff_13_q));  // open: Qn, preset, reset
  Multiplexer multiplexer_13 (.in0(d_ff_13_q), .in1(I_0), .out(multiplexer_13_out), .sel(decoder_1_out0));
  D_Flip_Flop #(.trigger("falling")) d_ff_14 (
    .D(multiplexer_14_out), .clk(RAM_clk_out), .Q(d_ff_14_q));  // open: Qn, preset, reset
  Multiplexer multiplexer_14 (.in0(d_ff_14_q), .in1(I_0), .out(multiplexer_14_out), .sel(decoder_1_out1));
  D_Flip_Flop #(.trigger("falling")) d_ff_15 (
    .D(multiplexer_15_out), .clk(RAM_clk_out), .Q(d_ff_15_q));  // open: Qn, preset, reset
  Multiplexer multiplexer_15 (.in0(d_ff_15_q), .in1(I_0), .out(multiplexer_15_out), .sel(decoder_1_out2));
  D_Flip_Flop #(.trigger("falling")) d_ff_16 (
    .D(multiplexer_16_out), .clk(RAM_clk_out), .Q(d_ff_16_q));  // open: Qn, preset, reset
  Multiplexer multiplexer_16 (.in0(d_ff_16_q), .in1(I_0), .out(multiplexer_16_out), .sel(decoder_1_out3));
  LED led_13 (.in(d_ff_13_q));
  LED led_14 (.in(d_ff_14_q));
  LED led_15 (.in(d_ff_15_q));
  LED led_16 (.in(d_ff_16_q));

  // Notes on the sheet:
  //   4x4 RAM
endmodule

module ram_4x1 (
  input  I,
  input  AD_En,
  input  [1:0] RAM_ad,
  output O_0,
  output O_1,
  output O_2,
  output O_3
);

  wire clock_1_out, decoder_1_out0, decoder_1_out1, decoder_1_out2, decoder_1_out3, multiplexer_1_out,
       multiplexer_2_out, multiplexer_3_out, multiplexer_4_out;

  Decoder #(.select(2)) decoder_1 (
    .out0(decoder_1_out0), .out1(decoder_1_out1), .out2(decoder_1_out2), .out3(decoder_1_out3), .sel(RAM_ad),
    .en(AD_En));
  Clock clock_1 (.out(clock_1_out));
  D_Flip_Flop #(.trigger("falling")) d_ff_1 (
    .D(multiplexer_1_out), .clk(clock_1_out), .Q(O_0));  // open: Qn, preset, reset
  Multiplexer multiplexer_1 (.in0(O_0), .in1(I), .out(multiplexer_1_out), .sel(decoder_1_out0));
  D_Flip_Flop #(.trigger("falling")) d_ff_2 (
    .D(multiplexer_2_out), .clk(clock_1_out), .Q(O_1));  // open: Qn, preset, reset
  Multiplexer multiplexer_2 (.in0(O_1), .in1(I), .out(multiplexer_2_out), .sel(decoder_1_out1));
  D_Flip_Flop #(.trigger("falling")) d_ff_3 (
    .D(multiplexer_3_out), .clk(clock_1_out), .Q(O_2));  // open: Qn, preset, reset
  Multiplexer multiplexer_3 (.in0(O_2), .in1(I), .out(multiplexer_3_out), .sel(decoder_1_out2));
  D_Flip_Flop #(.trigger("falling")) d_ff_4 (
    .D(multiplexer_4_out), .clk(clock_1_out), .Q(O_3));  // open: Qn, preset, reset
  Multiplexer multiplexer_4 (.in0(O_3), .in1(I), .out(multiplexer_4_out), .sel(decoder_1_out3));
  LED led_1 (.in(O_0));
  LED led_2 (.in(O_1));
  LED led_3 (.in(O_2));
  LED led_4 (.in(O_3));

  // Notes on the sheet:
  //   4x1 RAM
endmodule

module ram_4x2 (
  input  In_1,
  input  In_0,
  input  AD_En,
  input  [1:0] AD
);

  wire clock_1_out, d_ff_1_q, d_ff_2_q, d_ff_3_q, d_ff_4_q, d_ff_5_q, d_ff_6_q, d_ff_7_q, d_ff_8_q,
       decoder_1_out0, decoder_1_out1, decoder_1_out2, decoder_1_out3, multiplexer_1_out, multiplexer_2_out,
       multiplexer_3_out, multiplexer_4_out, multiplexer_5_out, multiplexer_6_out, multiplexer_7_out,
       multiplexer_8_out;

  Decoder #(.select(2)) decoder_1 (
    .out0(decoder_1_out0), .out1(decoder_1_out1), .out2(decoder_1_out2), .out3(decoder_1_out3), .sel(AD),
    .en(AD_En));
  Clock clock_1 (.out(clock_1_out));
  D_Flip_Flop #(.trigger("falling")) d_ff_1 (
    .D(multiplexer_1_out), .clk(clock_1_out), .Q(d_ff_1_q));  // open: Qn, preset, reset
  Multiplexer multiplexer_1 (.in0(d_ff_1_q), .in1(In_1), .out(multiplexer_1_out), .sel(decoder_1_out0));
  D_Flip_Flop #(.trigger("falling")) d_ff_2 (
    .D(multiplexer_2_out), .clk(clock_1_out), .Q(d_ff_2_q));  // open: Qn, preset, reset
  Multiplexer multiplexer_2 (.in0(d_ff_2_q), .in1(In_1), .out(multiplexer_2_out), .sel(decoder_1_out1));
  D_Flip_Flop #(.trigger("falling")) d_ff_3 (
    .D(multiplexer_3_out), .clk(clock_1_out), .Q(d_ff_3_q));  // open: Qn, preset, reset
  Multiplexer multiplexer_3 (.in0(d_ff_3_q), .in1(In_1), .out(multiplexer_3_out), .sel(decoder_1_out2));
  D_Flip_Flop #(.trigger("falling")) d_ff_4 (
    .D(multiplexer_4_out), .clk(clock_1_out), .Q(d_ff_4_q));  // open: Qn, preset, reset
  Multiplexer multiplexer_4 (.in0(d_ff_4_q), .in1(In_1), .out(multiplexer_4_out), .sel(decoder_1_out3));
  LED led_1 (.in(d_ff_1_q));
  LED led_2 (.in(d_ff_2_q));
  LED led_3 (.in(d_ff_3_q));
  LED led_4 (.in(d_ff_4_q));
  D_Flip_Flop #(.trigger("falling")) d_ff_5 (
    .D(multiplexer_5_out), .clk(clock_1_out), .Q(d_ff_5_q));  // open: Qn, preset, reset
  Multiplexer multiplexer_5 (.in0(d_ff_5_q), .in1(In_0), .out(multiplexer_5_out), .sel(decoder_1_out0));
  D_Flip_Flop #(.trigger("falling")) d_ff_6 (
    .D(multiplexer_6_out), .clk(clock_1_out), .Q(d_ff_6_q));  // open: Qn, preset, reset
  Multiplexer multiplexer_6 (.in0(d_ff_6_q), .in1(In_0), .out(multiplexer_6_out), .sel(decoder_1_out1));
  D_Flip_Flop #(.trigger("falling")) d_ff_7 (
    .D(multiplexer_7_out), .clk(clock_1_out), .Q(d_ff_7_q));  // open: Qn, preset, reset
  Multiplexer multiplexer_7 (.in0(d_ff_7_q), .in1(In_0), .out(multiplexer_7_out), .sel(decoder_1_out2));
  D_Flip_Flop #(.trigger("falling")) d_ff_8 (
    .D(multiplexer_8_out), .clk(clock_1_out), .Q(d_ff_8_q));  // open: Qn, preset, reset
  Multiplexer multiplexer_8 (.in0(d_ff_8_q), .in1(In_0), .out(multiplexer_8_out), .sel(decoder_1_out3));
  LED led_5 (.in(d_ff_5_q));
  LED led_6 (.in(d_ff_6_q));
  LED led_7 (.in(d_ff_7_q));
  LED led_8 (.in(d_ff_8_q));

  // Notes on the sheet:
  //   4x2 RAM
endmodule

module ram_2x1 (
  input  I,
  input  AD_En,
  input  AD
);

  wire clock_1_out, decoder_1_out0, decoder_1_out1, FF0_q, FF1_q, multiplexer_1_out, multiplexer_2_out;

  Decoder decoder_1 (.out0(decoder_1_out0), .out1(decoder_1_out1), .sel(AD), .en(AD_En));
  Clock clock_1 (.out(clock_1_out));
  Multiplexer multiplexer_1 (.in0(FF0_q), .in1(I), .out(multiplexer_1_out), .sel(decoder_1_out0));
  Multiplexer multiplexer_2 (.in0(FF1_q), .in1(I), .out(multiplexer_2_out), .sel(decoder_1_out1));
  D_Flip_Flop FF0 (.D(multiplexer_1_out), .clk(clock_1_out), .Q(FF0_q));  // open: Qn, preset, reset
  D_Flip_Flop FF1 (.D(multiplexer_2_out), .clk(clock_1_out), .Q(FF1_q));  // open: Qn, preset, reset
  LED led_1 (.in(FF0_q));
  LED led_2 (.in(FF1_q));

  // Notes on the sheet:
  //   2-bit memory
endmodule

module ram_1bit (
  input  in_1,
  input  in_2,
  input  in_3,
  input  in_4
);

  wire and_1_out, and_2_out, clock_1_out, clock_2_out, d_ff_1_q, d_ff_2_q, multiplexer_1_out, not_1_out,
       or_1_out;

  not not_1 (not_1_out, in_1);
  Multiplexer multiplexer_1 (.in0(d_ff_1_q), .in1(in_3), .out(multiplexer_1_out), .sel(in_4));
  Clock clock_1 (.out(clock_1_out));
  and and_1 (and_1_out, in_1, in_2);
  D_Flip_Flop d_ff_1 (.D(multiplexer_1_out), .clk(clock_1_out), .Q(d_ff_1_q));  // open: Qn, preset, reset
  and and_2 (and_2_out, d_ff_2_q, not_1_out);
  Clock clock_2 (.out(clock_2_out));
  D_Flip_Flop d_ff_2 (.D(or_1_out), .clk(clock_2_out), .Q(d_ff_2_q));  // open: Qn, preset, reset
  or or_1 (or_1_out, and_2_out, and_1_out);
  LED led_1 (.in(d_ff_1_q));
  LED led_2 (.in(d_ff_2_q));

  // Notes on the sheet:
  //   1-bit memory
  //   1-bit memory
endmodule
