// Logisim project ram_16x4.circ as structural Verilog: 3 circuits, main circuit register_4_bits
module main (
  input  I_3,
  input  I_2,
  input  I_1,
  input  I_0,
  input  [1:0] AD_MSB,
  input  [1:0] AD_LSB,
  input  R_W,
  input  En,
  output O_3,
  output O_2,
  output O_1,
  output O_0
);

  wire clock_1_out;

  Clock clock_1 (.out(clock_1_out));
  ram_16x4_better ram_16x4_better_1 (
    .AD_LESS(AD_LSB), .I_0(I_0), .I_1(I_1), .I_2(I_2), .I_3(I_3), .R_W(R_W), .En(En), .AD_MOSTE(AD_MSB),
    .RAM_clk(clock_1_out), .O_0(O_0), .O_1(O_1), .O_2(O_2), .O_3(O_3));
endmodule

module ram_16x4_better (
  input  [1:0] AD_LESS,
  input  I_0,
  input  I_1,
  input  I_2,
  input  I_3,
  input  R_W,
  input  En,
  input  [1:0] AD_MOSTE,
  input  RAM_clk,
  output O_0,
  output O_1,
  output O_2,
  output O_3
);

  wire and_1_out, and_2_out, and_3_out, and_4_out, and_5_out, and_6_out, and_7_out, and_8_out, and_9_out,
       and_10_out, and_11_out, and_12_out, and_13_out, and_14_out, and_15_out, and_16_out, and_17_out,
       and_18_out, and_19_out, and_20_out, and_21_out, and_22_out, and_23_out, and_24_out, and_25_out,
       and_26_out, and_27_out, and_28_out, and_29_out, and_30_out, and_31_out, and_32_out, and_33_out,
       and_34_out, decoder_1_out0, decoder_1_out1, decoder_1_out2, decoder_1_out3, decoder_2_out0,
       decoder_2_out1, decoder_2_out2, decoder_2_out3, decoder_3_out0, decoder_3_out1, decoder_3_out2,
       decoder_3_out3, decoder_4_out0, decoder_4_out1, decoder_4_out2, decoder_4_out3, not_1_out;
  wire [3:0] register_4_bits_1_o_0, register_4_bits_2_o_0, register_4_bits_3_o_0, register_4_bits_4_o_0,
       register_4_bits_5_o_0, register_4_bits_6_o_0, register_4_bits_7_o_0, register_4_bits_8_o_0,
       register_4_bits_9_o_0, register_4_bits_10_o_0, register_4_bits_11_o_0, register_4_bits_12_o_0,
       register_4_bits_13_o_0, register_4_bits_14_o_0, register_4_bits_15_o_0, register_4_bits_16_o_0;

  not not_1 (not_1_out, R_W);
  and and_1 (and_1_out, not_1_out, En);
  and and_2 (and_2_out, R_W, En);
  Decoder #(.select(2)) decoder_1 (
    .out0(decoder_1_out0), .out1(decoder_1_out1), .out2(decoder_1_out2), .out3(decoder_1_out3),
    .sel(AD_MOSTE), .en(and_2_out));
  Decoder #(.select(2)) decoder_2 (
    .out0(decoder_2_out0), .out1(decoder_2_out1), .out2(decoder_2_out2), .out3(decoder_2_out3),
    .sel(AD_MOSTE), .en(and_1_out));
  and and_3 (and_3_out, decoder_3_out0, decoder_2_out0);
  and and_4 (and_4_out, decoder_3_out0, decoder_2_out1);
  and and_5 (and_5_out, decoder_3_out0, decoder_2_out2);
  and and_6 (and_6_out, decoder_3_out0, decoder_2_out3);
  register_4_bits register_4_bits_1 (
    .I_0(I_0), .I_1(I_1), .I_2(I_2), .I_3(I_3), .S(and_3_out), .clk(RAM_clk), .O_3(register_4_bits_1_o_0[3]),
    .O_2(register_4_bits_1_o_0[2]), .O_1(register_4_bits_1_o_0[1]), .O_0(register_4_bits_1_o_0[0]));
  register_4_bits register_4_bits_2 (
    .I_0(I_0), .I_1(I_1), .I_2(I_2), .I_3(I_3), .S(and_4_out), .clk(RAM_clk), .O_3(register_4_bits_2_o_0[3]),
    .O_2(register_4_bits_2_o_0[2]), .O_1(register_4_bits_2_o_0[1]), .O_0(register_4_bits_2_o_0[0]));
  register_4_bits register_4_bits_3 (
    .I_0(I_0), .I_1(I_1), .I_2(I_2), .I_3(I_3), .S(and_5_out), .clk(RAM_clk), .O_3(register_4_bits_3_o_0[3]),
    .O_2(register_4_bits_3_o_0[2]), .O_1(register_4_bits_3_o_0[1]), .O_0(register_4_bits_3_o_0[0]));
  register_4_bits register_4_bits_4 (
    .I_0(I_0), .I_1(I_1), .I_2(I_2), .I_3(I_3), .S(and_6_out), .clk(RAM_clk), .O_3(register_4_bits_4_o_0[3]),
    .O_2(register_4_bits_4_o_0[2]), .O_1(register_4_bits_4_o_0[1]), .O_0(register_4_bits_4_o_0[0]));
  assign {O_3, O_2, O_1, O_0} = and_7_out ? register_4_bits_1_o_0 : 4'bz;  // Controlled_Buffer controlled_buffer_1
  and and_7 (and_7_out, decoder_4_out0, decoder_1_out0);
  assign {O_3, O_2, O_1, O_0} = and_8_out ? register_4_bits_2_o_0 : 4'bz;  // Controlled_Buffer controlled_buffer_2
  and and_8 (and_8_out, decoder_4_out0, decoder_1_out1);
  assign {O_3, O_2, O_1, O_0} = and_9_out ? register_4_bits_3_o_0 : 4'bz;  // Controlled_Buffer controlled_buffer_3
  and and_9 (and_9_out, decoder_4_out0, decoder_1_out2);
  assign {O_3, O_2, O_1, O_0} = and_10_out ? register_4_bits_4_o_0 : 4'bz;  // Controlled_Buffer controlled_buffer_4
  and and_10 (and_10_out, decoder_4_out0, decoder_1_out3);
  Decoder #(.select(2)) decoder_3 (
    .out0(decoder_3_out0), .out1(decoder_3_out1), .out2(decoder_3_out2), .out3(decoder_3_out3),
    .sel(AD_LESS), .en(and_1_out));
  and and_11 (and_11_out, decoder_3_out1, decoder_2_out0);
  and and_12 (and_12_out, decoder_3_out1, decoder_2_out1);
  and and_13 (and_13_out, decoder_3_out1, decoder_2_out2);
  and and_14 (and_14_out, decoder_3_out1, decoder_2_out3);
  Decoder #(.select(2)) decoder_4 (
    .out0(decoder_4_out0), .out1(decoder_4_out1), .out2(decoder_4_out2), .out3(decoder_4_out3),
    .sel(AD_LESS), .en(and_2_out));
  register_4_bits register_4_bits_5 (
    .I_0(I_0), .I_1(I_1), .I_2(I_2), .I_3(I_3), .S(and_11_out), .clk(RAM_clk),
    .O_3(register_4_bits_5_o_0[3]), .O_2(register_4_bits_5_o_0[2]), .O_1(register_4_bits_5_o_0[1]),
    .O_0(register_4_bits_5_o_0[0]));
  register_4_bits register_4_bits_6 (
    .I_0(I_0), .I_1(I_1), .I_2(I_2), .I_3(I_3), .S(and_12_out), .clk(RAM_clk),
    .O_3(register_4_bits_6_o_0[3]), .O_2(register_4_bits_6_o_0[2]), .O_1(register_4_bits_6_o_0[1]),
    .O_0(register_4_bits_6_o_0[0]));
  register_4_bits register_4_bits_7 (
    .I_0(I_0), .I_1(I_1), .I_2(I_2), .I_3(I_3), .S(and_13_out), .clk(RAM_clk),
    .O_3(register_4_bits_7_o_0[3]), .O_2(register_4_bits_7_o_0[2]), .O_1(register_4_bits_7_o_0[1]),
    .O_0(register_4_bits_7_o_0[0]));
  register_4_bits register_4_bits_8 (
    .I_0(I_0), .I_1(I_1), .I_2(I_2), .I_3(I_3), .S(and_14_out), .clk(RAM_clk),
    .O_3(register_4_bits_8_o_0[3]), .O_2(register_4_bits_8_o_0[2]), .O_1(register_4_bits_8_o_0[1]),
    .O_0(register_4_bits_8_o_0[0]));
  assign {O_3, O_2, O_1, O_0} = and_15_out ? register_4_bits_5_o_0 : 4'bz;  // Controlled_Buffer controlled_buffer_5
  and and_15 (and_15_out, decoder_4_out1, decoder_1_out0);
  assign {O_3, O_2, O_1, O_0} = and_16_out ? register_4_bits_6_o_0 : 4'bz;  // Controlled_Buffer controlled_buffer_6
  and and_16 (and_16_out, decoder_4_out1, decoder_1_out1);
  assign {O_3, O_2, O_1, O_0} = and_17_out ? register_4_bits_7_o_0 : 4'bz;  // Controlled_Buffer controlled_buffer_7
  and and_17 (and_17_out, decoder_4_out1, decoder_1_out2);
  assign {O_3, O_2, O_1, O_0} = and_18_out ? register_4_bits_8_o_0 : 4'bz;  // Controlled_Buffer controlled_buffer_8
  and and_18 (and_18_out, decoder_4_out1, decoder_1_out3);
  and and_19 (and_19_out, decoder_3_out2, decoder_2_out0);
  and and_20 (and_20_out, decoder_3_out2, decoder_2_out1);
  and and_21 (and_21_out, decoder_3_out2, decoder_2_out2);
  and and_22 (and_22_out, decoder_3_out2, decoder_2_out3);
  register_4_bits register_4_bits_9 (
    .I_0(I_0), .I_1(I_1), .I_2(I_2), .I_3(I_3), .S(and_19_out), .clk(RAM_clk),
    .O_3(register_4_bits_9_o_0[3]), .O_2(register_4_bits_9_o_0[1]), .O_1(register_4_bits_9_o_0[2]),
    .O_0(register_4_bits_9_o_0[0]));
  register_4_bits register_4_bits_10 (
    .I_0(I_0), .I_1(I_1), .I_2(I_2), .I_3(I_3), .S(and_20_out), .clk(RAM_clk),
    .O_3(register_4_bits_10_o_0[3]), .O_2(register_4_bits_10_o_0[1]), .O_1(register_4_bits_10_o_0[2]),
    .O_0(register_4_bits_10_o_0[0]));
  register_4_bits register_4_bits_11 (
    .I_0(I_0), .I_1(I_1), .I_2(I_2), .I_3(I_3), .S(and_21_out), .clk(RAM_clk),
    .O_3(register_4_bits_11_o_0[3]), .O_2(register_4_bits_11_o_0[1]), .O_1(register_4_bits_11_o_0[2]),
    .O_0(register_4_bits_11_o_0[0]));
  register_4_bits register_4_bits_12 (
    .I_0(I_0), .I_1(I_1), .I_2(I_2), .I_3(I_3), .S(and_22_out), .clk(RAM_clk),
    .O_3(register_4_bits_12_o_0[3]), .O_2(register_4_bits_12_o_0[1]), .O_1(register_4_bits_12_o_0[2]),
    .O_0(register_4_bits_12_o_0[0]));
  assign {O_3, O_2, O_1, O_0} = and_23_out ? register_4_bits_9_o_0 : 4'bz;  // Controlled_Buffer controlled_buffer_9
  and and_23 (and_23_out, decoder_4_out2, decoder_1_out0);
  assign {O_3, O_2, O_1, O_0} = and_24_out ? register_4_bits_10_o_0 : 4'bz;  // Controlled_Buffer controlled_buffer_10
  and and_24 (and_24_out, decoder_4_out2, decoder_1_out1);
  assign {O_3, O_2, O_1, O_0} = and_25_out ? register_4_bits_11_o_0 : 4'bz;  // Controlled_Buffer controlled_buffer_11
  and and_25 (and_25_out, decoder_4_out2, decoder_1_out2);
  assign {O_3, O_2, O_1, O_0} = and_26_out ? register_4_bits_12_o_0 : 4'bz;  // Controlled_Buffer controlled_buffer_12
  and and_26 (and_26_out, decoder_4_out2, decoder_1_out3);
  and and_27 (and_27_out, decoder_3_out3, decoder_2_out0);
  and and_28 (and_28_out, decoder_3_out3, decoder_2_out1);
  and and_29 (and_29_out, decoder_3_out3, decoder_2_out2);
  and and_30 (and_30_out, decoder_3_out3, decoder_2_out3);
  register_4_bits register_4_bits_13 (
    .I_0(I_0), .I_1(I_1), .I_2(I_2), .I_3(I_3), .S(and_27_out), .clk(RAM_clk),
    .O_3(register_4_bits_13_o_0[3]), .O_2(register_4_bits_13_o_0[2]), .O_1(register_4_bits_13_o_0[1]),
    .O_0(register_4_bits_13_o_0[0]));
  register_4_bits register_4_bits_14 (
    .I_0(I_0), .I_1(I_1), .I_2(I_2), .I_3(I_3), .S(and_28_out), .clk(RAM_clk),
    .O_3(register_4_bits_14_o_0[3]), .O_2(register_4_bits_14_o_0[2]), .O_1(register_4_bits_14_o_0[1]),
    .O_0(register_4_bits_14_o_0[0]));
  register_4_bits register_4_bits_15 (
    .I_0(I_0), .I_1(I_1), .I_2(I_2), .I_3(I_3), .S(and_29_out), .clk(RAM_clk),
    .O_3(register_4_bits_15_o_0[3]), .O_2(register_4_bits_15_o_0[2]), .O_1(register_4_bits_15_o_0[1]),
    .O_0(register_4_bits_15_o_0[0]));
  register_4_bits register_4_bits_16 (
    .I_0(I_0), .I_1(I_1), .I_2(I_2), .I_3(I_3), .S(and_30_out), .clk(RAM_clk),
    .O_3(register_4_bits_16_o_0[3]), .O_2(register_4_bits_16_o_0[2]), .O_1(register_4_bits_16_o_0[1]),
    .O_0(register_4_bits_16_o_0[0]));
  assign {O_3, O_2, O_1, O_0} = and_31_out ? register_4_bits_13_o_0 : 4'bz;  // Controlled_Buffer controlled_buffer_13
  and and_31 (and_31_out, decoder_4_out3, decoder_1_out0);
  assign {O_3, O_2, O_1, O_0} = and_32_out ? register_4_bits_14_o_0 : 4'bz;  // Controlled_Buffer controlled_buffer_14
  and and_32 (and_32_out, decoder_4_out3, decoder_1_out1);
  assign {O_3, O_2, O_1, O_0} = and_33_out ? register_4_bits_15_o_0 : 4'bz;  // Controlled_Buffer controlled_buffer_15
  and and_33 (and_33_out, decoder_4_out3, decoder_1_out2);
  assign {O_3, O_2, O_1, O_0} = and_34_out ? register_4_bits_16_o_0 : 4'bz;  // Controlled_Buffer controlled_buffer_16
  and and_34 (and_34_out, decoder_4_out3, decoder_1_out3);
endmodule

module register_4_bits (
  input  I_0,
  input  I_1,
  input  I_2,
  input  I_3,
  input  S,
  input  clk,
  output O_3,
  output O_2,
  output O_1,
  output O_0
);

  wire multiplexer_1_out, multiplexer_2_out, multiplexer_3_out, multiplexer_4_out;

  D_Flip_Flop #(.trigger("falling")) d_ff_1 (
    .D(multiplexer_1_out), .clk(clk), .Q(O_3), .preset(1'b0), .reset(1'b0));  // open: Qn
  Multiplexer multiplexer_1 (.in0(O_3), .in1(I_3), .out(multiplexer_1_out), .sel(S));
  Multiplexer multiplexer_2 (.in0(O_2), .in1(I_2), .out(multiplexer_2_out), .sel(S));
  D_Flip_Flop #(.trigger("falling")) d_ff_2 (
    .D(multiplexer_2_out), .clk(clk), .Q(O_2), .preset(1'b0), .reset(1'b0));  // open: Qn
  Multiplexer multiplexer_3 (.in0(O_1), .in1(I_1), .out(multiplexer_3_out), .sel(S));
  D_Flip_Flop #(.trigger("falling")) d_ff_3 (
    .D(multiplexer_3_out), .clk(clk), .Q(O_1), .preset(1'b0), .reset(1'b0));  // open: Qn
  Multiplexer multiplexer_4 (.in0(O_0), .in1(I_0), .out(multiplexer_4_out), .sel(S));
  D_Flip_Flop #(.trigger("falling")) d_ff_4 (
    .D(multiplexer_4_out), .clk(clk), .Q(O_0), .preset(1'b0), .reset(1'b0));  // open: Qn
endmodule
