// Logisim project register_file.circ as structural Verilog
module register_file (
  input  R1_En,
  input  [1:0] AD_R1,
  input  [3:0] I,
  input  W_En,
  input  [1:0] AD_W,
  input  R0_En,
  input  [1:0] AD_R0,
  input  clk,
  output [3:0] O_0,
  output [3:0] O_1
);

  wire decoder_1_out0, decoder_1_out1, decoder_1_out2, decoder_1_out3, decoder_2_out0, decoder_2_out1,
       decoder_2_out2, decoder_2_out3, decoder_3_out0, decoder_3_out1, decoder_3_out2, decoder_3_out3;
  wire [3:0] register_4_bits_1_o, register_4_bits_2_o, register_4_bits_3_o, register_4_bits_4_o;

  Decoder #(.select(2)) decoder_1 (
    .out0(decoder_1_out0), .out1(decoder_1_out1), .out2(decoder_1_out2), .out3(decoder_1_out3), .sel(AD_W),
    .en(W_En));
  Decoder #(.select(2)) decoder_2 (
    .out0(decoder_2_out0), .out1(decoder_2_out1), .out2(decoder_2_out2), .out3(decoder_2_out3), .sel(AD_R0),
    .en(R0_En));
  register_4_bits register_4_bits_1 (.I(I), .S(decoder_1_out0), .clk(clk), .O(register_4_bits_1_o));
  register_4_bits register_4_bits_2 (.I(I), .S(decoder_1_out1), .clk(clk), .O(register_4_bits_2_o));
  register_4_bits register_4_bits_3 (.I(I), .S(decoder_1_out2), .clk(clk), .O(register_4_bits_3_o));
  register_4_bits register_4_bits_4 (.I(I), .S(decoder_1_out3), .clk(clk), .O(register_4_bits_4_o));
  Decoder #(.select(2)) decoder_3 (
    .out0(decoder_3_out0), .out1(decoder_3_out1), .out2(decoder_3_out2), .out3(decoder_3_out3), .sel(AD_R1),
    .en(R1_En));
  assign O_0 = decoder_2_out0 ? register_4_bits_1_o : 4'bz;  // Controlled_Buffer controlled_buffer_1
  assign O_0 = decoder_2_out1 ? register_4_bits_2_o : 4'bz;  // Controlled_Buffer controlled_buffer_2
  assign O_0 = decoder_2_out2 ? register_4_bits_3_o : 4'bz;  // Controlled_Buffer controlled_buffer_3
  assign O_0 = decoder_2_out3 ? register_4_bits_4_o : 4'bz;  // Controlled_Buffer controlled_buffer_4
  assign O_1 = decoder_3_out0 ? register_4_bits_1_o : 4'bz;  // Controlled_Buffer controlled_buffer_5
  assign O_1 = decoder_3_out1 ? register_4_bits_2_o : 4'bz;  // Controlled_Buffer controlled_buffer_6
  assign O_1 = decoder_3_out2 ? register_4_bits_3_o : 4'bz;  // Controlled_Buffer controlled_buffer_7
  assign O_1 = decoder_3_out3 ? register_4_bits_4_o : 4'bz;  // Controlled_Buffer controlled_buffer_8
endmodule

module register_4_bits (
  input  [3:0] I,
  input  S,
  input  clk,
  output [3:0] O
);

  wire multiplexer_1_out, multiplexer_2_out, multiplexer_3_out, multiplexer_4_out;

  D_Flip_Flop #(.trigger("falling")) d_ff_1 (
    .D(multiplexer_1_out), .clk(clk), .Q(O[3]), .preset(1'b0), .reset(1'b0));  // open: Qn
  Multiplexer multiplexer_1 (.in0(O[3]), .in1(I[3]), .out(multiplexer_1_out), .sel(S));
  Multiplexer multiplexer_2 (.in0(O[2]), .in1(I[2]), .out(multiplexer_2_out), .sel(S));
  D_Flip_Flop #(.trigger("falling")) d_ff_2 (
    .D(multiplexer_2_out), .clk(clk), .Q(O[2]), .preset(1'b0), .reset(1'b0));  // open: Qn
  Multiplexer multiplexer_3 (.in0(O[1]), .in1(I[1]), .out(multiplexer_3_out), .sel(S));
  D_Flip_Flop #(.trigger("falling")) d_ff_3 (
    .D(multiplexer_3_out), .clk(clk), .Q(O[1]), .preset(1'b0), .reset(1'b0));  // open: Qn
  Multiplexer multiplexer_4 (.in0(O[0]), .in1(I[0]), .out(multiplexer_4_out), .sel(S));
  D_Flip_Flop #(.trigger("falling")) d_ff_4 (
    .D(multiplexer_4_out), .clk(clk), .Q(O[0]), .preset(1'b0), .reset(1'b0));  // open: Qn
endmodule
